# Fritzing sketch bmp280 (saved by Fritzing 0.9.5d)

parts:
  Компонент1 = Arduino Nano (Rev3.0)
  A1 = GY-BMP280 Breakout

nets:
  N1: Компонент1.GND, A1.Pin_2
  N2: Компонент1.A5, A1.Pin_3
  N3: Компонент1.A4, A1.Pin_4
  N4: Компонент1.3V3, A1.Pin_1
