# Fritzing sketch buzz_без_транзс (saved by Fritzing 0.9.5d)
breadboards: 1

parts:
  Компонент1 = Arduino Nano (Rev3.0)
  J1 = Piezo Speaker
  U1 = TRANSISTOR_NPN_2 [package=to-92]  # not connected

nets:
  N1: Компонент1.GND, J1.pin1
