# Fritzing sketch buzzer (saved by Fritzing 0.9.5d)

parts:
  Компонент1 = Passive Buzzer
  Компонент2 = Arduino Nano (Rev3.0)

nets:
  GND: Компонент1.GND, Компонент2.GND
  N1: Компонент1.S, Компонент2.D10
  N2: Компонент1.NC, Компонент2.3V3
