# Fritzing sketch mpu6050 (saved by Fritzing 0.9.5d)

parts:
  Компонент1 = Arduino Nano (Rev3.0)
  Компонент2 = InvenSense MPU6050

nets:
  GND: Компонент1.GND, Компонент2.GND
  N1: Компонент1.A5, Компонент2.SCL
  N2: Компонент1.A4, Компонент2.SDA
  3V3: Компонент1.3V3, Компонент2.VCC
