# Fritzing sketch sd (saved by Fritzing 0.9.5d)

parts:
  Компонент1 = Arduino Nano (Rev3.0)
  SD_card_module1 = SD Card Module

nets:
  N1: Компонент1.D11/MOSI, SD_card_module1.MOSI
  N2: Компонент1.D12/MISO, SD_card_module1.MISO
  GND: Компонент1.GND, SD_card_module1.GND
  N3: Компонент1.A0, SD_card_module1.CS
  N4: Компонент1.3V3, SD_card_module1.+3.3
  N5: Компонент1.D13/SCK, SD_card_module1.SCK

custom parts:
  SD Card Module: SD Card Module Slot Socket Reader For Arduino ARM MCU
